# Fritzing sketch schematics (saved by Fritzing 0.9.6b)
breadboards: 1

parts:
  Part1 = Real Time Clock Module - DS1307 RTC Breakout Board
  WeMos_D1_Mini1 = WeMos D1 Mini  # not connected
  S1 = Pushbutton [package="[SMD]"]
  Grove1 = Grove OLED 128x96
  VCC4 = 4 x AAA Battery Mount

nets:
  5V: Part1.5V, Grove1.VCC
  GND: Part1.GND, S1.Pin_1, S1.Pin_2, Grove1.GND, VCC4.-
  N1: S1.Pin_3, S1.Pin_4
